# Fritzing sketch psx232h (saved by Fritzing 0.9.3b)
breadboards: 1

parts:
  FT232h = Adafruit FT232H Breakout - USB C and STEMMA QT [part_number="Adafruit #2264"]
  ATF22V10C = IC, DIP package, 24 pins [chip_label=IC]
  H1 = polarizedheader 4pin 0.156in [package=THT]  # not connected
  H2 = polarizedheader 4pin 0.156in [package=THT]  # not connected
  H3 = polarizedheader 4pin 0.156in [package=THT]  # not connected

nets:
  N1: FT232h.GND, ATF22V10C.pin12
  N2: FT232h.+5V, ATF22V10C.pin24
  N3: FT232h.C0, ATF22V10C.pin21
  N4: FT232h.C2, ATF22V10C.pin23
  N5: FT232h.C3, ATF22V10C.pin22

notes:
  psx /rd
  psx /wr
  psx /cs0
  psx /reset
  psx A20
  psx D0
  psx D7
  psx232h , Uses ATF22V10C to introduce delay to the read/write signals

custom parts:
  Adafruit FT232H Breakout - USB C and STEMMA QT: Wouldn't it be cool to drive a tiny OLED display, read a color sensor, or even just flash some LEDs directly from your computer? Sure you can program an Arduino or Trinket to talk to these devices and your computer, but why can't your computer just talk to those devices and sensors itself? Well, now your computer can talk to devices using the Adafruit FT232H breakout board! What can the FT232H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
